# Fritzing sketch ArduinoAquariumControllerSchematic0_1a (saved by Fritzing 0.8.3b)
breadboards: 1

parts:
  J1 = Piezo Speaker  # not connected
  S1 = Momentary Switch [package=ksa_sealed_tac_switch]  # not connected
  DHT11 = Humidity and Temperature Sensor RHT03  # not connected
  LM35 = LM35 Temperature Sensor [package="TO92 [THT]"]  # not connected
  Fuse1 = Fuse with Handler [part_number=Htc-15m]  # not connected
  IC1 = DS1307 [package=THT]  # not connected
  S2 = Momentary Switch [package=ksa_sealed_tac_switch]  # not connected
  S3 = Momentary Switch [package=ksa_sealed_tac_switch]  # not connected
  S4 = Momentary Switch [package=ksa_sealed_tac_switch]  # not connected
  S5 = Momentary Switch [package=ksa_sealed_tac_switch]  # not connected
  Part1 = Arduino Mega 2560 (Rev3)
  LCD1 = LCD screen
  DS18B20 = LM35 Temperature Sensor [thermistor_type=NTC package="TO92 [THT]"]  # not connected

nets:
  N1: Part1.D21/SCL, LCD1.VDD
  N2: Part1.D20/SDA, LCD1.VSS
